# Fritzing sketch Transceiver Breakout (saved by Fritzing 0.8.3b)
circuit board: 1.3018cm x 1.29315cm
breadboards: 1

parts:
  J2 = female pin header, 4 pins [form="♀ (female)"]
  J3 = female pin header, 4 pins [form="♀ (female)"]
  J1 = female pin header, 4 pins [form="♀ (female)"]
  J4 = female pin header, 4 pins [form="♀ (female)"]

nets:
  N1: J2.pin1, J1.pin1
  N2: J2.pin2, J1.pin2
  N3: J2.pin3, J1.pin3
  N4: J2.pin4, J1.pin4
  N5: J3.pin1, J4.pin1
  N6: J3.pin2, J4.pin2
  N7: J3.pin3, J4.pin3
  N8: J3.pin4, J4.pin4
