# Fritzing sketch Beam Me Up (PCB) (saved by Fritzing 0.8.3b)
circuit board: 5.33115cm x 5.33cm

parts:
  R3 = Resistor [tolerance=±5% resistance=10k package=THT]
  ATMEGA = atmega328 [package=dip]
  M1 = DC Motor
  R5 = Resistor [tolerance=±5% resistance=10k package=THT]
  M4 = DC Motor
  Y1 = Resonator [frequency="16 Mhz" package=THT]
  R2 = Resistor [tolerance=±5% resistance=10k package=THT]
  M2 = DC Motor
  R4 = Resistor [tolerance=±5% resistance=10k package=THT]
  Q1 = NPN-Transistor [package="TO92 [THT]"]
  Q4 = NPN-Transistor [package="TO92 [THT]"]
  R1 = Resistor [tolerance=±5% resistance=10k package=THT]
  M3 = DC Motor
  Q2 = NPN-Transistor [package="TO92 [THT]"]
  J1 = female pin header, 2 pins [form="♀ (female)"]
  L1 = LED - 3mm [color="Red (633nm)" package="3 mm [THT]"]
  (C2) = Capacitor [package=cap-pth-small2]
  (C3) = Capacitor [package=cap-pth-small2]
  Q3 = NPN-Transistor [package="TO92 [THT]"]
  J2 = female pin header, 1 pin [form="♀ (female)"]
  J3 = female pin header, 1 pin [form="♀ (female)"]
  J4 = female pin header, 1 pin [form="♀ (female)"]
  J5 = female pin header, 1 pin [form="♀ (female)"]
  J6 = female pin header, 1 pin [form="♀ (female)"]
  J7 = female pin header, 1 pin [form="♀ (female)"]
  J8 = female pin header, 1 pin [form="♀ (female)"]
  J9 = female pin header, 1 pin [form="♀ (female)"]
  J10 = female pin header, 1 pin [form="♀ (female)"]
  J11 = female pin header, 1 pin [form="♀ (female)"]
  J12 = female pin header, 1 pin [form="♀ (female)"]
  J13 = female pin header, 1 pin [form="♀ (female)"]
  C1 = Electrolytic Capacitor [capacitance=10µF package="100 mil [THT, electrolytic]"]
  3_7V = Battery
  J14 = female pin header, 1 pin [form="♀ (female)"]
  J15 = female pin header, 1 pin [form="♀ (female)"]
  R6 = Resistor [tolerance=±5% resistance=10k package=THT]
  J16 = female pin header, 1 pin [form="♀ (female)"]
  J17 = female pin header, 1 pin [form="♀ (female)"]
  D4 = Diode [package=diode-1n4148]
  D1 = Diode [package=diode-1n4148]
  D2 = Diode [package=diode-1n4148]
  D3 = Diode [package=diode-1n4148]

nets:
  N1: R3.Pin_0, ATMEGA.D9_(PWM)
  N2: R3.Pin_1, Q3.B, J3.pin1
  N3: ATMEGA.RESET, R5.Pin_1
  N4: ATMEGA.D2, L1.cathode
  N5: ATMEGA.D3_(PWM), R1.Pin_1
  N6: ATMEGA.VCC, M1.pin_2, R5.Pin_0, M2.pin_2, J1.pin1, C1.+, 3_7V.+, R6.Pin_0, D1.C, D2.C
  GND: ATMEGA.GND, Y1.GND, Q1.E, Q4.E, Q2.E, (C2).1, (C3).1, Q3.E, J4.pin1, J7.pin1, J9.pin1, J12.pin1, C1.-, 3_7V.-
  N7: ATMEGA.XLAT1, Y1.0, (C2).2
  N8: ATMEGA.XLAT2, Y1.pin_1, (C3).2
  N9: ATMEGA.D6_(PWM), R4.Pin_1
  N10: ATMEGA.D10_(PWM), R2.Pin_0
  N11: ATMEGA.AVCC, ATMEGA.AREF, M4.pin_2, M3.pin_2, J1.pin2, D4.C, D3.C
  N12: M1.pin_1, Q1.C, J11.pin1, J16.pin1, D1.A
  N13: M4.pin_1, Q4.C, J8.pin1, J17.pin1, D4.A
  N14: R2.Pin_1, Q2.B, J6.pin1
  N15: M2.pin_1, Q2.C, J5.pin1, J14.pin1, D2.A
  N16: R4.Pin_0, Q4.B, J10.pin1
  N17: Q1.B, R1.Pin_0, J13.pin1
  N18: M3.pin_1, Q3.C, J2.pin1, J15.pin1, D3.A
  N19: L1.anode, R6.Pin_1

notes:
  +
  -
  D
  S
  G
  (Q4)
  (Q1)
  (Q2)
  (Q3)
  Quadcopter MKI
  'Beam Me Up'
