# Fritzing sketch Beam Me Up (Schematic) (saved by Fritzing 0.8.3b)

parts:
  U1 = atmega328 [package=dip]
  R5 = Resistor [tolerance=±5% resistance=10k package=THT]
  Y1 = Resonator [frequency="16 Mhz" package=THT]
  Q1 = NPN-Transistor [package="TO92 [THT]"]
  R1 = Resistor [tolerance=±5% resistance=10k package=THT]
  M1 = DC Motor
  M2 = DC Motor
  Q2 = NPN-Transistor [package="TO92 [THT]"]
  R2 = Resistor [tolerance=±5% resistance=10k package=THT]
  M3 = DC Motor
  Q3 = NPN-Transistor [package="TO92 [THT]"]
  R3 = Resistor [tolerance=±5% resistance=10k package=THT]
  M4 = DC Motor
  Q4 = NPN-Transistor [package="TO92 [THT]"]
  R4 = Resistor [tolerance=±5% resistance=10k package=THT]
  C1 = Electrolytic Capacitor [capacitance=10µF package="100 mil [THT, electrolytic]"]
  LED1 = LED - 3mm [color="Red (633nm)" package="3 mm [THT]"]
  R6 = Resistor [tolerance=±5% resistance=100 package=THT]
  D2 = Rectifier Diode [part_number=1N4001 package="300 mil [THT]"]
  D3 = Rectifier Diode [part_number=1N4001 package="300 mil [THT]"]
  D4 = Rectifier Diode [part_number=1N4001 package="300 mil [THT]"]
  D1 = Rectifier Diode [part_number=1N4001 package="300 mil [THT]"]

nets:
  N1: U1.RESET, R5.Pin_0
  N2: U1.D2, LED1.anode
  N3: U1.D3_(PWM), R1.Pin_0
  3.7V: U1.VCC, U1.AVCC, U1.AREF, R5.Pin_1, M1.pin_2, M2.pin_1, M3.pin_1, M4.pin_2, C1.+, D2.cathode, D3.cathode, D4.cathode, D1.cathode
  GND: U1.GND, Q1.E, Q2.E, Q3.E, Q4.E, C1.-, R6.Pin_1
  N4: U1.XLAT1, Y1.0
  N5: U1.XLAT2, Y1.pin_1
  N6: U1.D6_(PWM), R4.Pin_0
  N7: U1.D9_(PWM), R3.Pin_1
  N8: U1.D10_(PWM), R2.Pin_1
  N9: Q1.B, R1.Pin_1
  N10: Q1.C, M1.pin_1, D1.anode
  N11: M2.pin_2, Q2.C, D2.anode
  N12: Q2.B, R2.Pin_0
  N13: M3.pin_2, Q3.C, D3.anode
  N14: Q3.B, R3.Pin_0
  N15: M4.pin_1, Q4.C, D4.anode
  N16: Q4.B, R4.Pin_1
