# Fritzing sketch Ultrasonic_SimpleLCD (saved by Fritzing 0.8.3b)
breadboards: 1

parts:
  Part1 = Arduino Uno (Rev3)
  U2 = SPM0204UD5 [package=spm0204ud5]
  R1 = TRIMPOT [package=trim_pot_pth]
  U1 = LCD-16X2 [package=lcd-16x2]
  VCC1 = Battery block 9V

nets:
  GND: Part1.GND, U2.OUT, R1.CCW, U1.VSS, U1.R_W, U1.K, VCC1.-
  N1: Part1.D8, U1.RS
  N2: Part1.D11_PWM/MOSI, U2.GND
  N3: Part1.D12/MISO, U2.GND#
  N4: Part1.D3_PWM, U1.DB7
  N5: Part1.D4, U1.DB6
  N6: Part1.D5_PWM, U1.DB5
  N7: Part1.D6_PWM, U1.DB4
  N8: Part1.D7, U1.E
  5V: Part1.5V, U2.VS, R1.CW, U1.VDD, U1.A
  N9: Part1.VIN, VCC1.+

notes:
  SR04 Ultrasonic Sensor
